// Logisim project MUX.circ as structural Verilog: 1 circuit, main circuit main
module main (
  input  Z,
  input  [2:0] WXY
);

  wire multiplexer_1_out, multiplexer_2_out, multiplexer_3_out, multiplexer_4_out, multiplexer_5_out,
       multiplexer_6_out, multiplexer_7_out, multiplexer_8_out, not_1_out;

  not not_1 (not_1_out, Z);
  Multiplexer #(.select(3), .enable("false")) multiplexer_1 (
    .in0(Z), .in1(1'b1), .in2(Z), .in3(1'b0), .in4(not_1_out), .in5(1'b1), .in6(1'b0), .in7(1'b0),
    .out(multiplexer_1_out), .sel(WXY));
  Multiplexer #(.select(3), .enable("false")) multiplexer_2 (
    .in0(1'b1), .in1(1'b1), .in2(Z), .in3(1'b1), .in4(not_1_out), .in5(Z), .in6(1'b1), .in7(1'b0),
    .out(multiplexer_2_out), .sel(WXY));
  Multiplexer #(.select(3), .enable("false")) multiplexer_3 (
    .in0(1'b1), .in1(Z), .in2(1'b0), .in3(1'b1), .in4(not_1_out), .in5(Z), .in6(1'b1), .in7(1'b0),
    .out(multiplexer_3_out), .sel(WXY));
  Multiplexer #(.select(3), .enable("false")) multiplexer_4 (
    .in0(Z), .in1(1'b1), .in2(Z), .in3(1'b0), .in4(1'b0), .in5(1'b0), .in6(1'b0), .in7(1'b0),
    .out(multiplexer_4_out), .sel(WXY));
  Multiplexer #(.select(3), .enable("false")) multiplexer_5 (
    .in0(Z), .in1(1'b1), .in2(Z), .in3(1'b0), .in4(1'b0), .in5(1'b1), .in6(1'b0), .in7(1'b0),
    .out(multiplexer_5_out), .sel(WXY));
  Multiplexer #(.select(3), .enable("false")) multiplexer_6 (
    .in0(Z), .in1(Z), .in2(1'b0), .in3(1'b1), .in4(1'b0), .in5(1'b1), .in6(Z), .in7(1'b0),
    .out(multiplexer_6_out), .sel(WXY));
  Multiplexer #(.select(3), .enable("false")) multiplexer_7 (
    .in0(Z), .in1(not_1_out), .in2(Z), .in3(1'b1), .in4(1'b0), .in5(1'b1), .in6(Z), .in7(1'b0),
    .out(multiplexer_7_out), .sel(WXY));
  Multiplexer #(.select(3), .enable("false")) multiplexer_8 (
    .in0(1'b0), .in1(1'b0), .in2(not_1_out), .in3(1'b0), .in4(Z), .in5(1'b0), .in6(1'b0), .in7(1'b0),
    .out(multiplexer_8_out), .sel(WXY));
  _7_Segment_Display u_7_segment_display_1 (
    .g(multiplexer_7_out), .f(multiplexer_6_out), .a(multiplexer_1_out), .b(multiplexer_2_out),
    .e(multiplexer_5_out), .d(multiplexer_4_out), .c(multiplexer_3_out), .dp(multiplexer_8_out));

  // Notes on the sheet:
  //   a
  //   b
  //   c
  //   d
  //   e
  //   f
  //   g
  //   dot
  //   1820.2447.FAIY
endmodule
