// Logisim project SequentialCombinationalCircuit.circ as structural Verilog: 1 circuit, main circuit main
module main (
  input  in_1,
  output [2:0] out_2
);

  wire and_1_out, and_2_out, and_3_out, and_4_out, and_5_out, and_6_out, Clock_out, j_k_ff_1_q, j_k_ff_1_qn,
       j_k_ff_2_qn, j_k_ff_3_qn, multiplexer_1_out, multiplexer_2_out, multiplexer_3_out, multiplexer_4_out,
       multiplexer_5_out, multiplexer_6_out, multiplexer_7_out, multiplexer_8_out, not_1_out, not_2_out,
       or_1_out, or_2_out, or_3_out;

  Clock Clock (.out(Clock_out));
  not not_1 (not_1_out, in_1);
  not not_2 (not_2_out, j_k_ff_1_q);
  J_K_Flip_Flop j_k_ff_1 (
    .J(1'b1), .clk(Clock_out), .K(1'b1), .Q(j_k_ff_1_q), .Qn(j_k_ff_1_qn), .en(1'b1));  // open: preset, reset
  and and_1 (and_1_out, not_1_out, j_k_ff_1_q);
  and and_2 (and_2_out, j_k_ff_1_qn, in_1);
  or or_1 (or_1_out, and_1_out, and_2_out);
  J_K_Flip_Flop j_k_ff_2 (
    .J(or_1_out), .clk(Clock_out), .K(or_1_out), .Q(out_2[0]), .Qn(j_k_ff_2_qn), .en(1'b1));  // open: preset, reset
  Multiplexer #(.select(3), .enable("false")) multiplexer_1 (
    .in0(j_k_ff_1_q), .in1(1'b1), .in2(j_k_ff_1_q), .in3(1'b0), .in4(not_2_out), .in5(1'b1), .in6(1'b0),
    .in7(1'b0), .out(multiplexer_1_out), .sel(out_2));
  Multiplexer #(.select(3), .enable("false")) multiplexer_2 (
    .in0(1'b1), .in1(1'b1), .in2(j_k_ff_1_q), .in3(1'b1), .in4(not_2_out), .in5(j_k_ff_1_q), .in6(1'b1),
    .in7(1'b0), .out(multiplexer_2_out), .sel(out_2));
  Multiplexer #(.select(3), .enable("false")) multiplexer_3 (
    .in0(1'b1), .in1(j_k_ff_1_q), .in2(1'b0), .in3(1'b1), .in4(not_2_out), .in5(j_k_ff_1_q), .in6(1'b1),
    .in7(1'b0), .out(multiplexer_3_out), .sel(out_2));
  Multiplexer #(.select(3), .enable("false")) multiplexer_4 (
    .in0(j_k_ff_1_q), .in1(1'b1), .in2(j_k_ff_1_q), .in3(1'b0), .in4(1'b0), .in5(1'b0), .in6(1'b0),
    .in7(1'b0), .out(multiplexer_4_out), .sel(out_2));
  Multiplexer #(.select(3), .enable("false")) multiplexer_5 (
    .in0(j_k_ff_1_q), .in1(1'b1), .in2(j_k_ff_1_q), .in3(1'b0), .in4(1'b0), .in5(1'b1), .in6(1'b0),
    .in7(1'b0), .out(multiplexer_5_out), .sel(out_2));
  Multiplexer #(.select(3), .enable("false")) multiplexer_6 (
    .in0(j_k_ff_1_q), .in1(j_k_ff_1_q), .in2(1'b0), .in3(1'b1), .in4(1'b0), .in5(1'b1), .in6(j_k_ff_1_q),
    .in7(1'b0), .out(multiplexer_6_out), .sel(out_2));
  Multiplexer #(.select(3), .enable("false")) multiplexer_7 (
    .in0(j_k_ff_1_q), .in1(not_2_out), .in2(j_k_ff_1_q), .in3(1'b1), .in4(1'b0), .in5(1'b1),
    .in6(j_k_ff_1_q), .in7(1'b0), .out(multiplexer_7_out), .sel(out_2));
  Multiplexer #(.select(3), .enable("false")) multiplexer_8 (
    .in0(1'b0), .in1(1'b0), .in2(not_2_out), .in3(1'b0), .in4(j_k_ff_1_q), .in5(1'b0), .in6(1'b0),
    .in7(1'b0), .out(multiplexer_8_out), .sel(out_2));
  and and_3 (and_3_out, and_1_out, out_2[0]);
  and and_4 (and_4_out, j_k_ff_2_qn, and_2_out);
  or or_2 (or_2_out, and_3_out, and_4_out);
  J_K_Flip_Flop j_k_ff_3 (
    .J(or_2_out), .clk(Clock_out), .K(or_2_out), .Q(out_2[1]), .Qn(j_k_ff_3_qn), .en(1'b1));  // open: preset, reset
  and and_5 (and_5_out, and_3_out, out_2[1]);
  and and_6 (and_6_out, j_k_ff_3_qn, and_4_out);
  _7_Segment_Display u_7_segment_display_1 (
    .g(multiplexer_7_out), .f(multiplexer_6_out), .a(multiplexer_1_out), .b(multiplexer_2_out),
    .e(multiplexer_5_out), .d(multiplexer_4_out), .c(multiplexer_3_out), .dp(multiplexer_8_out));
  or or_3 (or_3_out, and_5_out, and_6_out);
  J_K_Flip_Flop j_k_ff_4 (
    .J(or_3_out), .clk(Clock_out), .K(or_3_out), .Q(out_2[2]), .en(1'b1));  // open: Qn, preset, reset

  // Notes on the sheet:
  //   a
  //   b
  //   c
  //   d
  //   e
  //   f
  //   g
  //   dot
  //   1820.2447.FAIY
endmodule
