// Logisim project decoder-combination.circ as structural Verilog: 1 circuit, main circuit main
module main (
  input  [3:0] in_1
);

  wire a_filter_2_out, a_filter_out, a_out, b_filter_2_out, b_filter_3_out, b_filter_out, b_out,
       c_filter_2_out, c_filter_out, c_out, d_filter_2_out, d_filter_out, d_out, decoder_1_out0,
       decoder_1_out1, decoder_1_out2, decoder_1_out3, decoder_1_out4, decoder_1_out5, decoder_1_out6,
       decoder_1_out7, decoder_1_out8, decoder_1_out9, decoder_1_out10, decoder_1_out11, decoder_1_out12,
       decoder_1_out13, decoder_1_out14, e_filter_2_out, e_filter_out, e_out, f_filter_2_out, f_filter_out,
       f_out, g_filter_2_out, g_filter_out, g_out, h_out;

  Decoder #(.select(4), .enable("false")) decoder_1 (
    .out0(decoder_1_out0), .out1(decoder_1_out1), .out2(decoder_1_out2), .out3(decoder_1_out3),
    .out4(decoder_1_out4), .out5(decoder_1_out5), .out6(decoder_1_out6), .out7(decoder_1_out7),
    .out8(decoder_1_out8), .out9(decoder_1_out9), .out10(decoder_1_out10), .out11(decoder_1_out11),
    .out12(decoder_1_out12), .out13(decoder_1_out13), .out14(decoder_1_out14), .sel(in_1));  // open: out15
  or b_filter (b_filter_out, decoder_1_out0, decoder_1_out1, decoder_1_out2, decoder_1_out3);
  or b_filter_2 (b_filter_2_out, decoder_1_out5, decoder_1_out6, decoder_1_out7, decoder_1_out8);
  or b_filter_3 (b_filter_3_out, decoder_1_out11, decoder_1_out12, decoder_1_out13);
  or e_filter (e_filter_out, decoder_1_out1, decoder_1_out2, decoder_1_out3, decoder_1_out5);
  or e_filter_2 (e_filter_2_out, decoder_1_out10, decoder_1_out11);
  or g_filter (g_filter_out, decoder_1_out1, decoder_1_out2, decoder_1_out5, decoder_1_out6, decoder_1_out7);
  or g_filter_2 (g_filter_2_out, decoder_1_out10, decoder_1_out11, decoder_1_out13);
  or a_filter (a_filter_out, decoder_1_out1, decoder_1_out2, decoder_1_out3, decoder_1_out5);
  or a_filter_2 (a_filter_2_out, decoder_1_out8, decoder_1_out11, decoder_1_out10);
  or c_filter (c_filter_out, decoder_1_out13, decoder_1_out0, decoder_1_out1, decoder_1_out12);
  or c_filter_2 (c_filter_2_out, decoder_1_out3, decoder_1_out6, decoder_1_out7, decoder_1_out8, decoder_1_out11);
  or d_filter (d_filter_out, decoder_1_out1, decoder_1_out2);
  or d_filter_2 (d_filter_2_out, decoder_1_out3, decoder_1_out5);
  or f_filter (f_filter_out, decoder_1_out1, decoder_1_out3, decoder_1_out6, decoder_1_out7);
  or f_filter_2 (f_filter_2_out, decoder_1_out10, decoder_1_out11, decoder_1_out13);
  or a (a_out, a_filter_out, a_filter_2_out);
  or b (b_out, b_filter_out, b_filter_2_out, b_filter_3_out);
  or c (c_out, c_filter_out, c_filter_2_out);
  or d (d_out, d_filter_out, d_filter_2_out);
  or e (e_out, e_filter_out, e_filter_2_out);
  or f (f_out, f_filter_out, f_filter_2_out);
  or g (g_out, g_filter_out, g_filter_2_out);
  or h (h_out, decoder_1_out4, decoder_1_out9, decoder_1_out14);
  _7_Segment_Display u_7_segment_display_1 (
    .g(g_out), .f(f_out), .a(a_out), .b(b_out), .e(e_out), .d(d_out), .c(c_out), .dp(h_out));

  // Notes on the sheet:
  //   1820.2447.FAIY
endmodule
